# Fritzing sketch greenhouse_v1.1.1 (saved by Fritzing 1.0.0rc)
circuit board: 10cm x 6cm
circuit board: 7cm x 10cm
circuit board: 8cm x 2cm
breadboards: 1

parts:
  DHT11_DIG = Humidity and Temperature Sensor DHT11  # not connected
  PWR = LED - 3mm [color="Green (565nm)" current=0.030A package="3 mm [THT]"]
  YL-69 = FC-28 Soil Hygrometer Module - Probe  # not connected
  TR_L = Basic FET N-Channel [package="TO220 [THT]"]
  PUMP = LED - 3mm [color="Green (565nm)" current=0.030A package="3 mm [THT]"]
  HEAT = LED - 3mm [color="Green (565nm)" current=0.030A package="3 mm [THT]"]
  R6 = Resistor [tolerance=±5% power=0.25W resistance=220 package=THT]
  R7 = Resistor [tolerance=±5% power=0.25W resistance=220 package=THT]
  R8 = Resistor [tolerance=±5% power=0.25W resistance=220 package=THT]
  R9 = Resistor [tolerance=±5% power=0.25W resistance=4.7k package=THT]
  PHOTO_R1 = PHOTOCELL [package=photocell]
  pot_T = Rotary Potentiometer (Large) [maximum_resistance=5kΩ knob_status=50% power=0.5W package=THT]
  pot_L = Rotary Potentiometer (Large) [maximum_resistance=5kΩ knob_status=50% power=0.5W package=THT]
  R10 = Resistor [tolerance=±5% power=0.25W resistance=4.7k package=THT]
  R11 = Resistor [tolerance=±5% power=0.25W resistance=4.7k package=THT]
  BTN_LAMP = Pushbutton [package="[THT]"]
  BTN_WLK = Pushbutton [package="[THT]"]
  BTN_DSPL = Pushbutton [package="[THT]"]
  PROXY_TANK = screw terminal, 2 pins
  Q3 = NPN-Transistor [package="TO92 [THT]"]
  pot_H = Rotary Potentiometer (Large) [maximum_resistance=5kΩ knob_status=50% power=0.5W package=THT]
  DHT11 = screw terminal, 3 pins
  RELAYS = screw terminal, 3 pins
  YL-70 = FC-28 Soil Hygrometer Module
  PHOTO_R = screw terminal, 2 pins
  DZ9v1 = DIODE-ZENER [package=diode-zener]
  R12 = Resistor [tolerance=±5% power=0.25W resistance=10 package=THT]
  LM7805-1 = Voltage Regulator - 5V [package="TO220 [THT]"]
  R13 = Resistor [tolerance=±5% power=0.25W resistance=10 package=THT]
  Arduino_NANO1 = Arduino Nano (Rev3.0)
  TR_P = Basic FET N-Channel [package="TO220 [THT]"]
  R14 = Resistor [tolerance=±5% power=0.25W resistance=10k package=THT]
  R15 = Resistor [tolerance=±5% power=0.25W resistance=10k package=THT]
  R16 = Resistor [tolerance=±5% power=0.25W resistance=10 package=THT]
  R17 = Resistor [tolerance=±5% power=0.25W resistance=10 package=THT]
  DS18B20 = screw terminal, 3 pins
  potenziomentri = screw terminal, 3 pins
  pot_pcb = screw terminal, 3 pins
  leds = screw terminal, 3 pins
  leds1 = screw terminal, 3 pins
  LM7805-2 = Voltage Regulator - 5V [package="TO220 [THT]"]
  PHOTO_R2 = screw terminal, 2 pins
  btn = screw terminal, 3 pins
  btn1 = screw terminal, 3 pins
  J1 = Power Jack [package=power_jack_pth]
  Pad1 = Pad [width=5 height=5 connect=center]  # not connected
  C1 = Tantalum Capacitor [capacitance=100nF voltage=16V package="100 mil [THT, tantalum]"]
  C2 = Tantalum Capacitor [capacitance=330nF voltage=16V package="100 mil [THT, tantalum]"]
  C4 = Tantalum Capacitor [capacitance=100nF voltage=16V package="100 mil [THT, tantalum]"]
  C3 = Tantalum Capacitor [capacitance=330nF voltage=16V package="100 mil [THT, tantalum]"]
  LCD = screw terminal, 2 pins
  DS1 = DS18B20 1-Wire Temperature Sensor [part_number=DS18B20]  # not connected
  5V = female pin header, 1 pin [form="♀ (female)"]
  lampVcc = female pin header, 1 pin [form="♀ (female)"]
  hygroVcc = female pin header, 1 pin [form="♀ (female)"]
  DS18Vcc = female pin header, 1 pin [form="♀ (female)"]
  LCDVcc = female pin header, 1 pin [form="♀ (female)"]
  DHT11Vcc = female pin header, 1 pin [form="♀ (female)"]
  heatRelayVcc = female pin header, 1 pin [form="♀ (female)"]

nets:
  GND: PWR.cathode, TR_L.source, PUMP.cathode, HEAT.cathode, R9.Pin_1, pot_T.leg1, pot_L.leg1, BTN_LAMP.Pin_1, BTN_LAMP.Pin_2, BTN_WLK.Pin_1, BTN_WLK.Pin_2, BTN_DSPL.Pin_2, PROXY_TANK.pin2, Q3.E, pot_H.leg1, DHT11.pin3, DZ9v1.A, Arduino_NANO1.GND, TR_P.source, R14.Pin_0, R15.Pin_0, DS18B20.pin3, J1.GND, J1.GNDBREAK, C1.-, C4.-
  N1: PWR.anode, R6.Pin_1
  N2: TR_L.gate, R14.Pin_1, R17.Pin_0
  N3: TR_L.drain, RELAYS.pin2
  N4: PUMP.anode, R7.Pin_1
  N5: HEAT.anode, R8.Pin_1
  N6: R6.Pin_0, leds1.pin3
  N7: R7.Pin_0, leds1.pin1
  N8: R8.Pin_0, leds1.pin2
  N9: R9.Pin_0, PHOTO_R.pin2, Arduino_NANO1.A0
  N10: PHOTO_R1.P$1, PHOTO_R2.pin1
  N11: PHOTO_R1.P$2, PHOTO_R2.pin2
  N12: pot_T.wiper, potenziomentri.pin1
  N13: pot_T.leg2, pot_L.leg2, pot_H.leg2
  N14: pot_L.wiper, potenziomentri.pin3
  N15: R10.Pin_0, Arduino_NANO1.A7
  N16: R10.Pin_1, Q3.B
  AN5v: R11.Pin_0, PHOTO_R.pin1, Arduino_NANO1.5V, 5V.pin1
  N17: R11.Pin_1, Arduino_NANO1.D7, DS18B20.pin2
  N18: BTN_LAMP.Pin_3, btn1.pin3
  N19: BTN_WLK.Pin_3, btn1.pin2
  N20: BTN_DSPL.Pin_3, btn1.pin1
  N21: PROXY_TANK.pin1, Arduino_NANO1.D2
  N22: Q3.C, YL-70.GND
  N23: pot_H.wiper, potenziomentri.pin2
  5V: DHT11.pin1, LM7805-1.output_voltage, DS18B20.pin1, C1.+, DS18Vcc.pin1, LCDVcc.pin1, DHT11Vcc.pin1, heatRelayVcc.pin1
  N24: DHT11.pin2, Arduino_NANO1.D6
  N25: RELAYS.pin1, Arduino_NANO1.D10
  N26: RELAYS.pin3, TR_P.drain
  5.1V: YL-70.VCC, LM7805-2.output_voltage, C4.+, lampVcc.pin1, hygroVcc.pin1
  N27: YL-70.AO, Arduino_NANO1.A6
  +9v1: DZ9v1.C, R13.Pin_1, Arduino_NANO1.VIN
  PUMP Vcc: R12.Pin_0, LM7805-1.input_voltage, LM7805-2.input_voltage, J1.PWR, C2.+, C3.+
  N28: R12.Pin_1, R13.Pin_0
  N29: LM7805-1.GND, C2.-
  N30: Arduino_NANO1.D3, btn.pin3
  N31: Arduino_NANO1.D4, btn.pin2
  N32: Arduino_NANO1.D5, btn.pin1
  N33: Arduino_NANO1.D8, R16.Pin_1
  N34: Arduino_NANO1.D9, R17.Pin_1
  N35: Arduino_NANO1.D11/MOSI, leds.pin3
  N36: Arduino_NANO1.D12/MISO, leds.pin2
  SCL: Arduino_NANO1.A5, LCD.pin2
  SDA: Arduino_NANO1.A4, LCD.pin1
  N37: Arduino_NANO1.A3, pot_pcb.pin1
  N38: Arduino_NANO1.A2, pot_pcb.pin2
  N39: Arduino_NANO1.A1, pot_pcb.pin3
  N40: Arduino_NANO1.D13/SCK, leds.pin1
  N41: TR_P.gate, R15.Pin_1, R16.Pin_0
  N42: LM7805-2.GND, C3.-

custom parts:
  Humidity and Temperature Sensor DHT11: Digital relative humidity & temperature sensor DHT11
  FC-28 Soil Hygrometer Module - Probe: The FC-28 is a soil hygrometer module that uses the Texas Instruments LM393 comparator chip to provide an analog measurement of soil humidity.
  FC-28 Soil Hygrometer Module: The FC-28 is a soil hygrometer module that uses the Texas Instruments LM393 comparator chip to provide an analog measurement of soil humidity. The digital output is high when soil moisture is over a certain threshold, as determined by adjusting the potentiometer.
