# Fritzing sketch greenhouse_v0.1.1 (saved by Fritzing 1.0.0rc)
breadboards: 1

parts:
  Arduino_NANO = Arduino Nano (Rev3.0)
  DHT11_DIG = Humidity and Temperature Sensor DHT11  # not connected
  PHOTO_R = PHOTOCELL [package=photocell]
  R2 = Temperature Sensor (Thermistor) [thermistor_type=NTC package=THT]  # not connected
  S1 = Pushbutton [package="[THT]"]
  LED1 = LED - 3mm [color="Orange (612nm)" current=0.030A package="3 mm [THT]"]  # not connected
  J1 = screw terminal, 2 pins
  V1 = DC Power [voltage=12V part_number=alimentatore]  # not connected
  R3 = Resistor [tolerance=±5% power=0.25W resistance=4.7k package=THT]
  S2 = Pushbutton [package="[THT]"]  # not connected
  YL-38 = FC-28 Soil Hygrometer Module
  YL-69 = FC-28 Soil Hygrometer Module - Probe
  Q1 = NPN-Transistor [package="SOT-23 [SMD]"]
  R4 = Resistor [tolerance=±5% power=0.25W resistance=4.7k package=THT]
  DS1 = DS18B20 1-Wire Temperature Sensor [part_number=DS18B20]
  R5 = Resistor [tolerance=±5% power=0.25W resistance=4.7k package=THT]

nets:
  GND: Arduino_NANO.GND, S1.Pin_2, J1.pin2, R3.Pin_1, Q1.2, DS1.GND
  N1: Arduino_NANO.D6, DS1.DQ, R5.Pin_1
  N2: Arduino_NANO.D8, S1.Pin_4
  N3: Arduino_NANO.D9, R4.Pin_1
  N4: Arduino_NANO.VIN, J1.pin1
  5V: Arduino_NANO.5V, PHOTO_R.P$1, YL-38.VCC, DS1.VDD, R5.Pin_0
  N5: Arduino_NANO.A1, YL-38.AO
  N6: Arduino_NANO.A0, PHOTO_R.P$2, R3.Pin_0
  N7: YL-38.GND, Q1.1
  N8: YL-38.POS, YL-69.POS
  N9: YL-38.NEG, YL-69.NEG
  N10: Q1.0, R4.Pin_0

custom parts:
  Humidity and Temperature Sensor DHT11: Digital relative humidity & temperature sensor DHT11
  FC-28 Soil Hygrometer Module: The FC-28 is a soil hygrometer module that uses the Texas Instruments LM393 comparator chip to provide an analog measurement of soil humidity. The digital output is high when soil moisture is over a certain threshold, as determined by adjusting the potentiometer.
  FC-28 Soil Hygrometer Module - Probe: The FC-28 is a soil hygrometer module that uses the Texas Instruments LM393 comparator chip to provide an analog measurement of soil humidity.
