# Fritzing sketch greenhouse_v0.1.2 (saved by Fritzing 1.0.0rc)
breadboards: 1

parts:
  Arduino_NANO = Arduino Nano (Rev3.0)
  DHT11_DIG = Humidity and Temperature Sensor DHT11  # not connected
  PHOTO_R = PHOTOCELL [package=photocell]
  R2 = Temperature Sensor (Thermistor) [thermistor_type=NTC package=THT]  # not connected
  S1 = Pushbutton [package="[THT]"]
  LED1 = LED - 3mm [color="Orange (612nm)" current=0.030A package="3 mm [THT]"]  # not connected
  J1 = screw terminal, 2 pins
  V1 = DC Power [voltage=12V part_number=alimentatore]  # not connected
  R3 = Resistor [tolerance=±5% power=0.25W resistance=4.7k package=THT]
  S2 = Pushbutton [package="[THT]"]  # not connected
  YL-69 = FC-28 Soil Hygrometer Module - Probe  # not connected
  R4 = Resistor [tolerance=±5% power=0.25W resistance=4.7k package=THT]
  DS1 = DS18B20 1-Wire Temperature Sensor [part_number=DS18B20]  # not connected
  R5 = Resistor [tolerance=±5% power=0.25W resistance=4.7k package=THT]
  DS18B20 = screw terminal, 3 pins
  DHT11 = screw terminal, 3 pins
  U1 = POT [knob_status=50% power=0.5W package=pot_alpha_rv16af-20]
  U2 = POT [knob_status=50% power=0.5W package=pot_alpha_rv16af-20]
  U3 = POT [knob_status=50% power=0.5W package=pot_alpha_rv16af-20]
  LED = screw terminal, 2 pins  # not connected
  PUMP = screw terminal, 2 pins  # not connected
  HEAT = screw terminal, 2 pins  # not connected
  YL-38 = FC-28 Soil Hygrometer Module  # not connected
  Q1 = npn-Powertransistor [package="TO220 [THT]"]

nets:
  GND: Arduino_NANO.GND, S1.Pin_2, J1.pin2, R3.Pin_1, DS18B20.pin3, DHT11.pin3, U1.E, U2.E, U3.E, Q1.emitter
  N1: Arduino_NANO.D5, DHT11.pin2
  N2: Arduino_NANO.D6, R5.Pin_1, DS18B20.pin2
  N3: Arduino_NANO.D8, S1.Pin_4
  N4: Arduino_NANO.D9, R4.Pin_1
  N5: Arduino_NANO.VIN, J1.pin1
  N6: Arduino_NANO.5V, PHOTO_R.P$1, R5.Pin_0, DS18B20.pin1, DHT11.pin1, U1.A, U2.A, U3.A
  N7: Arduino_NANO.A7, U3.S
  N8: Arduino_NANO.A6, U2.S
  N9: Arduino_NANO.A5, U1.S
  N10: Arduino_NANO.A0, PHOTO_R.P$2, R3.Pin_0
  N11: R4.Pin_0, Q1.base

custom parts:
  Humidity and Temperature Sensor DHT11: Digital relative humidity & temperature sensor DHT11
  FC-28 Soil Hygrometer Module - Probe: The FC-28 is a soil hygrometer module that uses the Texas Instruments LM393 comparator chip to provide an analog measurement of soil humidity.
  FC-28 Soil Hygrometer Module: The FC-28 is a soil hygrometer module that uses the Texas Instruments LM393 comparator chip to provide an analog measurement of soil humidity. The digital output is high when soil moisture is over a certain threshold, as determined by adjusting the potentiometer.
