# Fritzing sketch greenhouse_v1.1.0 (saved by Fritzing 1.0.0rc)
circuit board: 10cm x 6cm
circuit board: 8cm x 2cm
circuit board: 10cm x 7cm
breadboards: 1

parts:
  DHT11_DIG = Humidity and Temperature Sensor DHT11
  PWR = LED - 3mm [color="Green (565nm)" current=0.030A package="3 mm [THT]"]
  YL-69 = FC-28 Soil Hygrometer Module - Probe  # not connected
  DS1 = DS18B20 1-Wire Temperature Sensor [part_number=DS18B20]
  Q2 = Basic FET N-Channel [package="TO220 [THT]"]
  PUMP = LED - 3mm [color="Green (565nm)" current=0.030A package="3 mm [THT]"]
  HEAT = LED - 3mm [color="Green (565nm)" current=0.030A package="3 mm [THT]"]
  R6 = Resistor [tolerance=±5% power=0.25W resistance=220 package=THT]
  R7 = Resistor [tolerance=±5% power=0.25W resistance=220 package=THT]
  R8 = Resistor [tolerance=±5% power=0.25W resistance=220 package=THT]
  R9 = Resistor [tolerance=±5% power=0.25W resistance=4.7k package=THT]
  PHOTO_R1 = PHOTOCELL [package=photocell]
  pot_T = Rotary Potentiometer (Large) [maximum_resistance=5kΩ knob_status=50% power=0.5W package=THT]
  pot_L = Rotary Potentiometer (Large) [maximum_resistance=5kΩ knob_status=50% power=0.5W package=THT]
  R10 = Resistor [tolerance=±5% power=0.25W resistance=4.7k package=THT]
  R11 = Resistor [tolerance=±5% power=0.25W resistance=4.7k package=THT]
  BTN_LAMP = Pushbutton [package="[THT]"]
  BTN_WLK = Pushbutton [package="[THT]"]
  BTN_DSPL = Pushbutton [package="[THT]"]
  LCD = screw terminal, 4 pins
  PROXY_TANK = screw terminal, 2 pins
  Q3 = NPN-Transistor [package="TO92 [THT]"]
  pot_H = Rotary Potentiometer (Large) [maximum_resistance=5kΩ knob_status=50% power=0.5W package=THT]
  DHT11 = screw terminal, 3 pins
  RELAYS = screw terminal, 3 pins
  YL-70 = FC-28 Soil Hygrometer Module
  PHOTO_R = screw terminal, 2 pins
  Pad1 = Pad [width=5 height=5 connect=center]  # not connected
  DZ9v1 = DIODE-ZENER [package=diode-zener]
  R12 = Resistor [tolerance=±5% power=0.25W resistance=10 package=THT]
  LM7805-1 = Voltage Regulator - 5V [package="TO220 [THT]"]
  C1 = Electrolytic Capacitor [capacitance=100nF voltage=16V package="100 mil [THT, electrolytic]"]
  C2 = Electrolytic Capacitor [capacitance=330nF voltage=16V package="100 mil [THT, electrolytic]"]
  Power_12V = Power plug
  R13 = Resistor [tolerance=±5% power=0.25W resistance=10 package=THT]
  Arduino_NANO1 = Arduino Nano (Rev3.0)
  Q4 = Basic FET N-Channel [package="TO220 [THT]"]
  R14 = Resistor [tolerance=±5% power=0.25W resistance=10k package=THT]
  R15 = Resistor [tolerance=±5% power=0.25W resistance=10k package=THT]
  R16 = Resistor [tolerance=±5% power=0.25W resistance=10 package=THT]
  R17 = Resistor [tolerance=±5% power=0.25W resistance=10 package=THT]
  DS18B20 = screw terminal, 3 pins
  potenziomentri = screw terminal, 3 pins
  potenziomentri_pcb = screw terminal, 3 pins
  leds = screw terminal, 3 pins
  leds1 = screw terminal, 3 pins
  LM7805-2 = Voltage Regulator - 5V [package="TO220 [THT]"]
  C3 = Electrolytic Capacitor [capacitance=330nF voltage=16V package="100 mil [THT, electrolytic]"]
  C4 = Electrolytic Capacitor [capacitance=100nF voltage=16V package="100 mil [THT, electrolytic]"]
  PHOTO_R2 = screw terminal, 2 pins
  btn = screw terminal, 3 pins
  btn1 = screw terminal, 3 pins

nets:
  5V/DHT11 Vcc/DS18B20 Vcc/HEAT RELAY Vcc/HYGRO Vcc/LAMP Vcc/LCD Vcc: DHT11_DIG.Vcc, DS1.VDD, LCD.pin1, DHT11.pin1, YL-70.VCC, LM7805-1.output_voltage, C1.+, DS18B20.pin1, LM7805-2.output_voltage, C4.+
  GND: DHT11_DIG.GND_2, PWR.cathode, DS1.GND, Q2.source, PUMP.cathode, HEAT.cathode, R9.Pin_1, pot_T.leg1, pot_L.leg1, BTN_LAMP.Pin_1, BTN_LAMP.Pin_2, BTN_WLK.Pin_1, BTN_WLK.Pin_2, BTN_DSPL.Pin_2, LCD.pin4, PROXY_TANK.pin2, Q3.E, pot_H.leg1, DHT11.pin3, DZ9v1.A, C1.-, Power_12V.GND, Arduino_NANO1.GND, Q4.source, R14.Pin_0, R15.Pin_0, DS18B20.pin3, C4.-
  N1: PWR.anode, R6.Pin_1
  N2: Q2.gate, R14.Pin_1, R17.Pin_0
  N3: Q2.drain, RELAYS.pin2
  N4: PUMP.anode, R7.Pin_1
  N5: HEAT.anode, R8.Pin_1
  N6: R6.Pin_0, leds1.pin3
  N7: R7.Pin_0, leds1.pin1
  N8: R8.Pin_0, leds1.pin2
  N9: R9.Pin_0, PHOTO_R.pin2, Arduino_NANO1.A0
  N10: PHOTO_R1.P$1, PHOTO_R2.pin1
  N11: PHOTO_R1.P$2, PHOTO_R2.pin2
  N12: pot_T.wiper, potenziomentri.pin1
  AN5v: pot_T.leg2, pot_L.leg2, R11.Pin_0, pot_H.leg2, PHOTO_R.pin1, Arduino_NANO1.5V
  N13: pot_L.wiper, potenziomentri.pin3
  N14: R10.Pin_0, Arduino_NANO1.A7
  N15: R10.Pin_1, Q3.B
  N16: R11.Pin_1, Arduino_NANO1.D7, DS18B20.pin2
  N17: BTN_LAMP.Pin_3, btn1.pin3
  N18: BTN_WLK.Pin_3, btn1.pin2
  N19: BTN_DSPL.Pin_3, btn1.pin1
  N20: LCD.pin2, Arduino_NANO1.A4
  N21: LCD.pin3, Arduino_NANO1.A5
  N22: PROXY_TANK.pin1, Arduino_NANO1.D2
  N23: Q3.C, YL-70.GND
  N24: pot_H.wiper, potenziomentri.pin2
  N25: DHT11.pin2, Arduino_NANO1.D6
  N26: RELAYS.pin1, Arduino_NANO1.D10
  N27: RELAYS.pin3, Q4.drain
  N28: YL-70.AO, Arduino_NANO1.A6
  +9v1: DZ9v1.C, R13.Pin_1, Arduino_NANO1.VIN
  PUMP Vcc: R12.Pin_0, LM7805-1.input_voltage, C2.+, Power_12V.VCC, LM7805-2.input_voltage, C3.+
  N29: R12.Pin_1, R13.Pin_0
  N30: LM7805-1.GND, C2.-
  N31: Arduino_NANO1.D3, btn.pin3
  N32: Arduino_NANO1.D4, btn.pin2
  N33: Arduino_NANO1.D5, btn.pin1
  N34: Arduino_NANO1.D8, R16.Pin_1
  N35: Arduino_NANO1.D9, R17.Pin_1
  N36: Arduino_NANO1.D11/MOSI, leds.pin3
  N37: Arduino_NANO1.D12/MISO, leds.pin2
  N38: Arduino_NANO1.A3, potenziomentri_pcb.pin1
  N39: Arduino_NANO1.A2, potenziomentri_pcb.pin2
  N40: Arduino_NANO1.A1, potenziomentri_pcb.pin3
  N41: Arduino_NANO1.D13/SCK, leds.pin1
  N42: Q4.gate, R15.Pin_1, R16.Pin_0
  N43: LM7805-2.GND, C3.-

custom parts:
  Humidity and Temperature Sensor DHT11: Digital relative humidity & temperature sensor DHT11
  FC-28 Soil Hygrometer Module - Probe: The FC-28 is a soil hygrometer module that uses the Texas Instruments LM393 comparator chip to provide an analog measurement of soil humidity.
  FC-28 Soil Hygrometer Module: The FC-28 is a soil hygrometer module that uses the Texas Instruments LM393 comparator chip to provide an analog measurement of soil humidity. The digital output is high when soil moisture is over a certain threshold, as determined by adjusting the potentiometer.
