# Fritzing sketch greenhouse_v1.2.6 (saved by Fritzing 1.0.0rc)
circuit board: 8cm x 2cm
circuit board: 10cm x 6cm
circuit board: 7cm x 10cm
breadboards: 1

parts:
  PWR = LED - 3mm [color="Green (565nm)" current=0.030A package="3 mm [THT]"]
  YL-69 = FC-28 Soil Hygrometer Module - Probe  # not connected
  TR_L = Basic FET N-Channel [package="TO220 [THT]"]
  PUMP = LED - 3mm [color="Green (565nm)" current=0.030A package="3 mm [THT]"]
  HEAT = LED - 3mm [color="Green (565nm)" current=0.030A package="3 mm [THT]"]
  R6 = Resistor [tolerance=±5% power=0.25W resistance=220 package=THT]
  R7 = Resistor [tolerance=±5% power=0.25W resistance=220 package=THT]
  R8 = Resistor [tolerance=±5% power=0.25W resistance=220 package=THT]
  R9 = Resistor [tolerance=±5% power=0.25W resistance=4.7k package=THT]
  PHOTO_R1 = PHOTOCELL [package=photocell]
  pot_T = Rotary Potentiometer (Large) [maximum_resistance=5kΩ knob_status=50% power=0.5W package=THT]
  pot_L = Rotary Potentiometer (Large) [maximum_resistance=5kΩ knob_status=50% power=0.5W package=THT]
  R10 = Resistor [tolerance=±5% power=0.25W resistance=4.7k package=THT]
  R11 = Resistor [tolerance=±5% power=0.25W resistance=4.7k package=THT]
  BTN_LAMP = Pushbutton [package="[THT]"]
  BTN_WLK = Pushbutton [package="[THT]"]
  BTN_DSPL = Pushbutton [package="[THT]"]
  TANK = screw terminal, 2 pins
  Q3 = NPN-Transistor [package="TO92 [THT]"]
  pot_H = Rotary Potentiometer (Large) [maximum_resistance=5kΩ knob_status=50% power=0.5W package=THT]
  DHT11 = screw terminal, 3 pins
  PHOTO = screw terminal, 2 pins
  DZ9v1 = DIODE-ZENER [package=diode-zener]
  R12 = Resistor [tolerance=±5% power=0.25W resistance=10 package=THT]
  LM7805-1 = Voltage Regulator - 5V [package="TO220 [THT]"]
  R13 = Resistor [tolerance=±5% power=0.25W resistance=10 package=THT]
  TR_P = Basic FET N-Channel [package="TO220 [THT]"]
  R14 = Resistor [tolerance=±5% power=0.25W resistance=10k package=THT]
  R15 = Resistor [tolerance=±5% power=0.25W resistance=10k package=THT]
  R16 = Resistor [tolerance=±5% power=0.25W resistance=10 package=THT]
  R17 = Resistor [tolerance=±5% power=0.25W resistance=10 package=THT]
  DS18B20 = screw terminal, 3 pins
  leds1 = screw terminal, 3 pins
  LM7805-2 = Voltage Regulator - 5V [package="TO220 [THT]"]
  PHOTO_R2 = screw terminal, 2 pins
  btn1 = screw terminal, 3 pins
  12V = Power Jack [package=power_jack_pth]
  Pad1 = Pad [width=9.533242903722277 height=4.8522423833263755 connect=center]  # not connected
  DS1 = DS18B20 1-Wire Temperature Sensor [part_number=DS18B20]  # not connected
  LCDVcc = female pin header, 1 pin [form="♀ (female)"]
  RELAYS = screw terminal, 6 pins
  Pad2 = Pad [width=7.902222222222222 height=9.03111111111111 connect=center]
  potenziomentri = screw terminal, 4 pins
  LCDSDA = female pin header, 1 pin [form="♀ (female)"]
  LCDSCL = female pin header, 1 pin [form="♀ (female)"]
  DHT11_DIG = Humidity and Temperature Sensor DHT11  # not connected
  YL-70 = FC-28 Soil Hygrometer Module
  Arduino_NANO1 = Arduino Nano (Rev3.0)
  GND = female pin header, 1 pin [form="♀ (female)"]
  AN5V = female pin header, 1 pin [form="♀ (female)"]
  pot1 = female pin header, 1 pin [form="♀ (female)"]
  pot2 = female pin header, 1 pin [form="♀ (female)"]
  pot3 = female pin header, 1 pin [form="♀ (female)"]
  btn_lamp = female pin header, 1 pin [form="♀ (female)"]
  btn_wlk = female pin header, 1 pin [form="♀ (female)"]
  btn_dspl = female pin header, 1 pin [form="♀ (female)"]
  C7 = Ceramic Capacitor [capacitance=100nF voltage=16V package="200 mil [THT, multilayer]"]
  C8 = Electrolytic Capacitor [capacitance=0.47mF voltage=16V package="100 mil [THT, electrolytic]"]
  C9 = Electrolytic Capacitor [capacitance=0.47mF voltage=16V package="100 mil [THT, electrolytic]"]
  C10 = Electrolytic Capacitor [capacitance=1mF voltage=16V package="200 mil [THT, electrolytic]"]
  R18 = Resistor [tolerance=±5% power=0.25W resistance=4.7 package=THT]
  C11 = Ceramic Capacitor [capacitance=100nF voltage=16V package="200 mil [THT, multilayer]"]
  C12 = Ceramic Capacitor [capacitance=300nF voltage=16V package="200 mil [THT, multilayer]"]
  C13 = Ceramic Capacitor [capacitance=100nF voltage=16V package="200 mil [THT, multilayer]"]
  C14 = Ceramic Capacitor [capacitance=300nF voltage=16V package="200 mil [THT, multilayer]"]
  L_PWR = female pin header, 1 pin [form="♀ (female)"]
  L_HEAT = female pin header, 1 pin [form="♀ (female)"]
  L_PUMP = female pin header, 1 pin [form="♀ (female)"]
  Vcc = female pin header, 1 pin [form="♀ (female)"]

nets:
  GND: PWR.cathode, TR_L.source, PUMP.cathode, HEAT.cathode, R9.Pin_1, pot_T.leg1, pot_L.leg1, BTN_LAMP.Pin_1, BTN_LAMP.Pin_2, BTN_WLK.Pin_1, BTN_WLK.Pin_2, BTN_DSPL.Pin_2, TANK.pin1, Q3.E, pot_H.leg1, DHT11.pin2, DZ9v1.A, LM7805-1.GND, TR_P.source, R14.Pin_0, R15.Pin_0, DS18B20.pin3, LM7805-2.GND, 12V.GND, 12V.GNDBREAK, Pad2.pad, Arduino_NANO1.GND, GND.pin1, C7.0, C8.-, C9.-, C10.-, C11.0, C12.0, C13.0, C14.0
  N1: PWR.anode, R6.Pin_1
  N2: TR_L.gate, R14.Pin_1, R17.Pin_0
  LAMP gnd: TR_L.drain, RELAYS.pin4
  N3: PUMP.anode, R7.Pin_1
  N4: HEAT.anode, R8.Pin_1
  N5: R6.Pin_0, leds1.pin3
  N6: R7.Pin_0, leds1.pin1
  N7: R8.Pin_0, leds1.pin2
  N8: R9.Pin_0, PHOTO.pin2, Arduino_NANO1.A0
  N9: PHOTO_R1.P$1, PHOTO_R2.pin1
  N10: PHOTO_R1.P$2, PHOTO_R2.pin2
  N11: pot_T.wiper, potenziomentri.pin3
  N12: pot_T.leg2, pot_L.leg2, pot_H.leg2, potenziomentri.pin4
  N13: pot_L.wiper, potenziomentri.pin1
  N14: R10.Pin_0, Arduino_NANO1.A7
  N15: R10.Pin_1, Q3.B
  AN5v: R11.Pin_0, PHOTO.pin1, Arduino_NANO1.5V, AN5V.pin1
  N16: R11.Pin_1, DS18B20.pin2, Arduino_NANO1.D12/MISO
  N17: BTN_LAMP.Pin_3, btn1.pin3
  N18: BTN_WLK.Pin_3, btn1.pin2
  N19: BTN_DSPL.Pin_3, btn1.pin1
  N20: TANK.pin2, Arduino_NANO1.D11/MOSI
  N21: Q3.C, YL-70.GND
  N22: pot_H.wiper, potenziomentri.pin2
  DHT11 Vcc/DS18B20 Vcc/HYGRO Vcc/LCD Vcc: DHT11.pin1, DS18B20.pin1, LM7805-2.output_voltage, LCDVcc.pin1, YL-70.VCC, C8.+, C11.1, Vcc.pin1
  N23: DHT11.pin3, Arduino_NANO1.D13/SCK
  +9v1: DZ9v1.C, R13.Pin_1, Arduino_NANO1.VIN, C7.1
  PUMP Vcc: R12.Pin_0, LM7805-1.input_voltage, LM7805-2.input_voltage, 12V.PWR, RELAYS.pin6, C10.+, C12.1, C14.1
  N24: R12.Pin_1, R18.Pin_0
  HEAT RELAY Vcc/LAMP Vcc: LM7805-1.output_voltage, RELAYS.pin2, RELAYS.pin5, C9.+, C13.1
  N25: R13.Pin_0, R18.Pin_1
  N26: TR_P.gate, R15.Pin_1, R16.Pin_0
  PUMP gnd: TR_P.drain, RELAYS.pin3
  N27: R16.Pin_1, Arduino_NANO1.D9
  N28: R17.Pin_1, Arduino_NANO1.D10
  HEAT RELAY sig: RELAYS.pin1, Arduino_NANO1.D2
  N29: LCDSDA.pin1, Arduino_NANO1.A4
  N30: LCDSCL.pin1, Arduino_NANO1.A5
  N31: YL-70.AO, Arduino_NANO1.A6
  N32: Arduino_NANO1.D3, btn_lamp.pin1
  N33: Arduino_NANO1.D4, btn_wlk.pin1
  N34: Arduino_NANO1.D5, btn_dspl.pin1
  N35: Arduino_NANO1.D6, L_PUMP.pin1
  N36: Arduino_NANO1.D7, L_HEAT.pin1
  N37: Arduino_NANO1.D8, L_PWR.pin1
  N38: Arduino_NANO1.A3, pot3.pin1
  N39: Arduino_NANO1.A2, pot2.pin1
  N40: Arduino_NANO1.A1, pot1.pin1

notes:
  PMP+
  LAMP+
  LAMP-
  PMP-
  REL.H.Vcc
  REL.H.sign
  REL.Vcc

custom parts:
  FC-28 Soil Hygrometer Module - Probe: The FC-28 is a soil hygrometer module that uses the Texas Instruments LM393 comparator chip to provide an analog measurement of soil humidity.
  Humidity and Temperature Sensor DHT11: Digital relative humidity & temperature sensor DHT11
  FC-28 Soil Hygrometer Module: The FC-28 is a soil hygrometer module that uses the Texas Instruments LM393 comparator chip to provide an analog measurement of soil humidity. The digital output is high when soil moisture is over a certain threshold, as determined by adjusting the potentiometer.
